# Fritzing sketch Design 01 - Spaghetti (saved by Fritzing 0.9.4)

parts:
  R1 = Photocell (LDR) [package=THT]
  DHT1 = DHT22 Humidity and Temperature Sensor
  Part1 = Soil Moisture Sensor
  Part2 = Arduino Uno (Rev3)
  R2 = Resistor [tolerance=±5% resistance=5.6k package=THT]
  Part8 = Bluetooth HC-05 Macho
  Part9 = I2C level shifter bidirectional

nets:
  VDD: R1.pin_0, DHT1.VDD, Part1.VCC, Part2.5V, Part9.HV
  N1: R1.pin_1, Part2.A0, R2.Pin_0
  N2: DHT1.DATA, Part2.D7
  GND: DHT1.GND, Part1.GND, Part2.GND, R2.Pin_1, Part8.Key, Part8.GND, Part9.GND
  N3: Part1.SIG, Part2.A1
  N4: Part2.D10_PWM/SS, Part9.HV4
  N5: Part2.D11_PWM/MOSI, Part9.HV3
  3V3: Part2.3V3, Part8.VCC, Part9.LV
  N6: Part8.TXD, Part9.LV3
  N7: Part8.RXD, Part9.LV4
