# Fritzing sketch Design 02 - Breadboarded (saved by Fritzing 0.9.4)
breadboards: 1

parts:
  R1 = Resistor [tolerance=±5% resistance=5.6k package=THT]
  R2 = Photocell (LDR) [package=THT]
  Part1 = Bluetooth HC-05 Macho
  Part2 = I2C level shifter bidirectional
  Part3 = Arduino Uno (Rev3)
  Part4 = Soil Moisture Sensor
  DHT1 = DHT22 Humidity and Temperature Sensor

nets:
  GND: R1.Pin_0, Part1.Key, Part1.GND, Part2.GND, Part3.GND, Part4.GND, DHT1.GND
  N1: R1.Pin_1, R2.pin_0, Part3.A0
  5V: R2.pin_1, Part2.HV, Part3.5V, Part4.VCC, DHT1.VDD
  N2: Part1.TXD, Part2.LV2
  N3: Part1.RXD, Part2.LV1
  VCC: Part1.VCC, Part2.LV, Part3.3V3
  N4: Part2.HV1, Part3.D10_PWM/SS
  N5: Part2.HV2, Part3.D11_PWM/MOSI
  N6: Part3.A1, Part4.SIG
  N7: Part3.D7, DHT1.DATA
