# Fritzing sketch Testers (saved by Fritzing 0.9.4)

parts:
  DHT1 = DHT22 Humidity and Temperature Sensor
  Part1 = Arduino Uno (Rev3)
  Part2 = Arduino Uno (Rev3)
  Part3 = Soil Moisture Sensor
  Part4 = Arduino Uno (Rev3)
  R1 = Photocell (LDR) [package=THT]
  R2 = Resistor [tolerance=±5% resistance=5.6k package=THT]
  Part5 = Bluetooth HC-05 Macho
  Part6 = Arduino Uno (Rev3)
  Part7 = I2C level shifter bidirectional

nets:
  VDD: DHT1.VDD, Part1.5V
  N1: DHT1.DATA, Part1.D2
  GND: DHT1.GND, Part1.GND
  N2: Part2.A0, Part3.SIG
  5V: Part2.5V, Part3.VCC
  GND_2: Part2.GND, Part3.GND
  N3: Part4.A0, R1.pin_0, R2.Pin_0
  N4: Part4.5V, R1.pin_1
  N5: Part4.GND, R2.Pin_1
  N6: Part5.TXD, Part7.LV3
  N7: Part5.RXD, Part7.LV4
  VCC: Part5.VCC, Part6.3V3, Part7.LV
  GND_3: Part5.Key, Part5.GND, Part6.GND, Part7.GND
  N8: Part6.D10_PWM/SS, Part7.HV4
  N9: Part6.D11_PWM/MOSI, Part7.HV3
  N10: Part6.5V, Part7.HV
